// Logisim project CPU.circ as structural Verilog: 10 circuits, main circuit main
module main (
  input  in_1
);

  wire CLK, E, ex_1_isbranch, isBeq, isBgt, isCall, isImm, isLd, isRet, isSt, isUbranch;
  wire [2:0] FlagIn, FlagOut;
  wire [3:0] A, ofetch_1_a1, ofetch_1_a2, rd, register_file_1_r0_out_2, register_file_1_r0_out_3,
       register_file_1_r0_out_4;
  wire [12:0] AluSignal;
  wire [19:0] register_file_1_r0_out;
  wire [31:0] AluResult, D, ex_1_branchpc, ifetch_1_instruction, LdResult, multiplexer_2_out,
       ofetch_1_branchtarget, ofetch_1_immx, Op1, Op2, PC;

  Clock clock_1 (.out(CLK));
  Hex_Digit_Display hex_digit_display_1 (.value(register_file_1_r0_out_4));  // open: dp
  // Probe on ifetch_1_instruction
  Hex_Digit_Display hex_digit_display_2 (.value(register_file_1_r0_out_3));  // open: dp
  Hex_Digit_Display hex_digit_display_3 (.value(register_file_1_r0_out_2));  // open: dp
  Hex_Digit_Display hex_digit_display_4 (.value(register_file_1_r0_out[19:16]));  // open: dp
  Hex_Digit_Display hex_digit_display_5 (.value(register_file_1_r0_out[15:12]));  // open: dp
  // Probe on D
  Hex_Digit_Display hex_digit_display_6 (.value(register_file_1_r0_out[11:8]));  // open: dp
  Hex_Digit_Display hex_digit_display_7 (.value(register_file_1_r0_out[7:4]));  // open: dp
  Hex_Digit_Display hex_digit_display_8 (.value(register_file_1_r0_out[3:0]));  // open: dp
  IFetch ifetch_1 (
    .IsBranch(ex_1_isbranch), .BranchPC(ex_1_branchpc), .CLK(CLK), .reset(in_1),
    .Instruction(ifetch_1_instruction), .PCout(PC));
  oFetch ofetch_1 (
    .isSt(isSt), .isRet(isRet), .Instruction(ifetch_1_instruction), .PC(PC), .Immx(ofetch_1_immx),
    .A1(ofetch_1_a1), .A2(ofetch_1_a2), .rd(rd), .BranchTarget(ofetch_1_branchtarget));
  Ex ex_1 (
    .isRet(isRet), .BranchTarget(ofetch_1_branchtarget), .Flag(FlagOut), .isBeq(isBeq), .op1(Op1),
    .isUbranch(isUbranch), .isBgt(isBgt), .BranchPC(ex_1_branchpc), .isBranch(ex_1_isbranch));
  ControlUnit controlunit_1 (
    .Instruction(ifetch_1_instruction), .IsImmediate(isImm), .AluSignals(AluSignal), .IsLd(isLd),
    .IsSt(isSt), .IsBeq(isBeq), .IsBgt(isBgt), .IsCall(isCall), .IsRet(isRet), .IsWb(E), .IsUbranch(isUbranch));
  Multiplexer #(.width(4)) multiplexer_1 (.in0(rd), .in1(4'b1111), .out(A), .sel(isCall));
  // Probe on PC
  // Probe on Op1
  // Probe on Op2
  Register_File register_file_1 (
    .A1(ofetch_1_a1), .A2(ofetch_1_a2), .A(A), .CLK(CLK), .Reset(in_1), .E(E), .D(D),
    .r0_out({register_file_1_r0_out_4, register_file_1_r0_out_3, register_file_1_r0_out_2, register_file_1_r0_out}),
    .D1(Op1), .D2(Op2));
  Multiplexer #(.width(32)) multiplexer_2 (.in0(Op2), .in1(ofetch_1_immx), .out(multiplexer_2_out), .sel(isImm));
  Register #(.width(3)) Flags (.D(FlagIn), .en(1'b1), .clk(CLK), .Q(FlagOut));  // open: clr
  // Probe on multiplexer_2_out
  MA ma_1 (.isLd(isLd), .isSt(isSt), .CLK(CLK), .AluResult(AluResult), .Op2(Op2), .LdResult(LdResult));
  RW rw_1 (.isCall(isCall), .aluResult(AluResult), .PC(PC), .isLd(isLd), .ldResult(LdResult), .D(D));
  ALU alu_1 (
    .AluSignal(AluSignal), .Reg_A(Op1), .Flag_prev(FlagOut), .Reg_B(multiplexer_2_out), .Dout(AluResult),
    .Flag(FlagIn));
  Comparator #(.width(3)) comparator_1 (.a(FlagIn), .b(FlagOut));  // open: gt, eq, lt
  // Probe on D

  // Other names for the same wires on the sheet: reset = in_1
endmodule

module IFetch (
  input  IsBranch,
  input  [31:0] BranchPC,
  input  CLK,
  input  reset,
  output [31:0] Instruction,
  output [31:0] PCout
);

  wire controlled_buffer_1_out, nand_1_out;
  wire [31:0] adder_1_out, multiplexer_1_out;

  // Probe on multiplexer_1_out
  Register #(.width(32)) PC (.D(multiplexer_1_out), .en(1'b1), .clk(controlled_buffer_1_out), .Q(PCout), .clr(reset));
  assign controlled_buffer_1_out = nand_1_out ? CLK : 1'bz;  // Controlled_Buffer controlled_buffer_1
  Multiplexer #(.width(32)) multiplexer_1 (.in0(adder_1_out), .in1(BranchPC), .out(multiplexer_1_out), .sel(IsBranch));
  Adder #(.width(32)) adder_1 (.a(32'h1), .b(PCout), .out(adder_1_out));  // open: cin, cout
  ROM #(.addrWidth(16), .dataWidth(32)) Instruction_Memory_0469d480 (.addr(PCout[15:0]), .data(Instruction));
  nand nand_1 (nand_1_out, Instruction[31], Instruction[30], Instruction[29], Instruction[28], Instruction[27], Instruction[26], Instruction[25], Instruction[24], Instruction[23], Instruction[22], Instruction[21], Instruction[20], Instruction[19], Instruction[18], Instruction[17], Instruction[16], Instruction[15], Instruction[14], Instruction[13], Instruction[12], Instruction[11], Instruction[10], Instruction[9], Instruction[8], Instruction[7], Instruction[6], Instruction[5], Instruction[4], Instruction[3], Instruction[2], Instruction[1], Instruction[0]);

  // Other names for the same wires on the sheet: clock = CLK

  // Notes on the sheet:
  //   contents of Instruction_Memory_0469d480 (hex, n*v repeats v):
  //   98000008 68000000 68000000 4d00000a 4d400037 1914000 9d50000 12150000 4c800026 4cc00045 18cc8000
  //   a0000000
endmodule

module oFetch (
  input  isSt,
  input  isRet,
  input  [31:0] Instruction,
  input  [31:0] PC,
  output [31:0] Immx,
  output [3:0] A1,
  output [3:0] A2,
  output [3:0] rd,
  output [31:0] BranchTarget
);

  wire [31:0] bit_extender_1_out, bit_extender_2_out, bit_extender_3_out, shifter_1_out;

  assign bit_extender_1_out = {{5{Instruction[26]}}, Instruction[26:0]};  // Bit_Extender bit_extender_1
  assign bit_extender_2_out = {{16{Instruction[15]}}, Instruction[15:0]};  // Bit_Extender bit_extender_2
  assign bit_extender_3_out = {{16{1'b0}}, Instruction[15:0]};  // Bit_Extender bit_extender_3
  Adder #(.width(32)) adder_1 (.a(bit_extender_1_out), .b(PC), .out(BranchTarget));  // open: cin, cout
  Shifter #(.width(32)) shifter_1 (.in(bit_extender_3_out), .\dist (5'b10000), .out(shifter_1_out));
  Multiplexer #(.select(2), .width(32)) multiplexer_1 (
    .in0(bit_extender_2_out), .in1(bit_extender_3_out), .in2(shifter_1_out), .out(Immx),
    .sel(Instruction[17:16]));  // open: in3
  Multiplexer #(.width(4)) multiplexer_2 (.in0(Instruction[21:18]), .in1(4'b1111), .out(A1), .sel(isRet));
  Multiplexer #(.width(4)) multiplexer_3 (.in0(Instruction[17:14]), .in1(Instruction[25:22]), .out(A2), .sel(isSt));

  assign rd = Instruction[25:22];
endmodule

module Ex (
  input  isRet,
  input  [31:0] BranchTarget,
  input  [2:0] Flag,
  input  isBeq,
  input  [31:0] op1,
  input  isUbranch,
  input  isBgt,
  output [31:0] BranchPC,
  output isBranch
);

  wire and_1_out, and_2_out, nor_1_out;

  and and_1 (and_1_out, isBeq, Flag[1]);
  nor nor_1 (nor_1_out, Flag[2], Flag[1]);
  and and_2 (and_2_out, isBgt, nor_1_out);
  or or_1 (isBranch, isUbranch, and_1_out, and_2_out);
  Multiplexer #(.width(32)) multiplexer_1 (.in0(BranchTarget), .in1(op1), .out(BranchPC), .sel(isRet));

  // Notes on the sheet:
  //   Flag.E
  //   Flag.GT
endmodule

module MA (
  input  isLd,
  input  isSt,
  input  CLK,
  input  [31:0] AluResult,
  input  [31:0] Op2,
  output [31:0] LdResult
);

  RAM #(.addrWidth(16), .dataWidth(32)) ram_1 (
    .addr(AluResult[15:0]), .we(isSt), .oe(isLd), .clk(CLK), .din(Op2), .dout(LdResult));
endmodule

module RW (
  input  isCall,
  input  [31:0] aluResult,
  input  [31:0] PC,
  input  isLd,
  input  [31:0] ldResult,
  output [31:0] D
);

  wire [31:0] adder_1_out;

  Adder #(.width(32)) adder_1 (.a(PC), .b(32'h1), .out(adder_1_out));  // open: cin, cout
  Multiplexer #(.select(2), .width(32)) multiplexer_1 (
    .in0(aluResult), .in1(ldResult), .in2(adder_1_out), .out(D), .sel({isCall, isLd}));  // open: in3
endmodule

module ControlUnit (
  input  [31:0] Instruction,
  output IsImmediate,
  output [12:0] AluSignals,
  output IsLd,
  output IsSt,
  output IsBeq,
  output IsBgt,
  output IsCall,
  output IsRet,
  output IsWb,
  output IsUbranch
);

  wire and_1_out, and_2_out, and_3_out, and_4_out, demultiplexer_1_out0, demultiplexer_1_out18, nor_1_out,
       not_1_out, not_2_out, not_3_out, not_4_out, not_5_out, or_1_out, or_2_out;

  Demultiplexer #(.select(5)) demultiplexer_1 (
    .out0(demultiplexer_1_out0), .out1(AluSignals[1]), .out2(AluSignals[2]), .out3(AluSignals[3]),
    .out4(AluSignals[4]), .out5(AluSignals[5]), .out6(AluSignals[6]), .out7(AluSignals[7]),
    .out8(AluSignals[8]), .out9(AluSignals[9]), .out10(AluSignals[10]), .out11(AluSignals[11]),
    .out12(AluSignals[12]), .out14(IsLd), .out15(IsSt), .out16(IsBeq), .out17(IsBgt),
    .out18(demultiplexer_1_out18), .out19(IsCall), .out20(IsRet), .in(1'b1), .sel(Instruction[31:27]));  // open: out13, out21, out22, out23, out24, out25, out26, out27, out28, out29, out30, out31
  not not_1 (not_1_out, Instruction[27]);
  not not_2 (not_2_out, Instruction[28]);
  not not_3 (not_3_out, Instruction[29]);
  not not_4 (not_4_out, Instruction[30]);
  not not_5 (not_5_out, Instruction[31]);
  and and_1 (and_1_out, not_5_out, Instruction[30], Instruction[29], Instruction[28]);
  or or_1 (or_1_out, not_2_out, Instruction[30]);
  and and_2 (and_2_out, not_1_out, not_2_out, Instruction[29]);
  and and_3 (and_3_out, Instruction[28], not_3_out);
  or or_2 (or_2_out, and_2_out, and_3_out);
  or or_3 (AluSignals[0], demultiplexer_1_out0, and_1_out);
  and and_4 (and_4_out, Instruction[27], or_1_out, Instruction[29], not_5_out);
  nor nor_1 (nor_1_out, and_4_out, Instruction[31]);
  or or_4 (IsWb, IsCall, nor_1_out);
  and and_5 (IsUbranch, or_2_out, not_4_out, Instruction[31]);

  assign IsImmediate = Instruction[26];

  // Notes on the sheet:
  //   Instruction
  //   IsImmediate
  //   Is Add
  //   IsSub
  //   IsMul
  //   IsDiv
  //   IsMod
  //   IsCmp
  //   IsAnd
  //   IsOr
  //   IsNot
  //   IsMov
  //   IsLsl
  //   IsLsr
  //   IsAsr
  //   IsLd
  //   IsSt
  //   IsBeq
  //   IsBgt
  //   IsCall
  //   IsRet
  //   Is Add
  //   IsWb
  //   IsUbranch
endmodule

module ALU (
  input  [12:0] AluSignal,
  input  [31:0] Reg_A,
  input  [2:0] Flag_prev,
  input  [31:0] Reg_B,
  output [31:0] Dout,
  output [2:0] Flag
);

  wire adder_1_cout, comparator_1_eq, comparator_1_gt, comparator_1_lt, or_1_out, subtractor_1_bout;
  wire [3:0] Choose;
  wire [4:0] controlled_buffer_12_out, controlled_buffer_14_out, controlled_buffer_16_out;
  wire [31:0] adder_1_out, and_1_out, controlled_buffer_1_out, controlled_buffer_2_out,
       controlled_buffer_3_out, controlled_buffer_4_out, controlled_buffer_5_out, controlled_buffer_6_out,
       controlled_buffer_7_out, controlled_buffer_8_out, controlled_buffer_9_out, controlled_buffer_10_out,
       controlled_buffer_11_out, controlled_buffer_13_out, controlled_buffer_15_out,
       controlled_buffer_17_out, controlled_buffer_18_out, controlled_buffer_19_out,
       controlled_buffer_20_out, controlled_buffer_21_out, controlled_inverter_1_out, divider_1_out,
       divider_1_rem, multiplier_1_out, or_2_out, shifter_1_out, shifter_2_out, shifter_3_out,
       subtractor_1_out;

  or or_1 (or_1_out, AluSignal[4], AluSignal[3]);
  assign controlled_buffer_1_out = AluSignal[0] ? Reg_A : 32'bz;  // Controlled_Buffer controlled_buffer_1
  Adder #(.width(32)) adder_1 (
    .a(controlled_buffer_1_out), .b(controlled_buffer_2_out), .out(adder_1_out), .cout(adder_1_cout));  // open: cin
  assign controlled_buffer_2_out = AluSignal[0] ? Reg_B : 32'bz;  // Controlled_Buffer controlled_buffer_2
  assign controlled_buffer_3_out = AluSignal[1] ? Reg_A : 32'bz;  // Controlled_Buffer controlled_buffer_3
  Subtractor #(.width(32)) subtractor_1 (
    .a(controlled_buffer_3_out), .b(controlled_buffer_4_out), .out(subtractor_1_out), .bout(subtractor_1_bout));  // open: bin
  assign controlled_buffer_4_out = AluSignal[1] ? Reg_B : 32'bz;  // Controlled_Buffer controlled_buffer_4
  assign controlled_buffer_5_out = AluSignal[5] ? Reg_A : 32'bz;  // Controlled_Buffer controlled_buffer_5
  Comparator #(.width(32)) comparator_1 (
    .a(controlled_buffer_5_out), .b(controlled_buffer_6_out), .gt(comparator_1_gt), .eq(comparator_1_eq),
    .lt(comparator_1_lt));
  assign controlled_buffer_6_out = AluSignal[5] ? Reg_B : 32'bz;  // Controlled_Buffer controlled_buffer_6
  assign controlled_buffer_7_out = AluSignal[2] ? Reg_A : 32'bz;  // Controlled_Buffer controlled_buffer_7
  Multiplier #(.width(32)) multiplier_1 (
    .a(controlled_buffer_7_out), .b(controlled_buffer_8_out), .out(multiplier_1_out));  // open: cin, cout
  assign controlled_buffer_8_out = AluSignal[2] ? Reg_B : 32'bz;  // Controlled_Buffer controlled_buffer_8
  assign controlled_buffer_9_out = or_1_out ? Reg_A : 32'bz;  // Controlled_Buffer controlled_buffer_9
  Divider #(.width(32)) divider_1 (
    .a(controlled_buffer_9_out), .b(controlled_buffer_10_out), .out(divider_1_out), .rem(divider_1_rem));  // open: upper
  assign controlled_buffer_10_out = or_1_out ? Reg_B : 32'bz;  // Controlled_Buffer controlled_buffer_10
  assign controlled_buffer_11_out = AluSignal[10] ? Reg_A : 32'bz;  // Controlled_Buffer controlled_buffer_11
  Shifter #(.width(32)) shifter_1 (
    .in(controlled_buffer_11_out), .\dist (controlled_buffer_12_out), .out(shifter_1_out));
  assign controlled_buffer_12_out = AluSignal[10] ? Reg_B[4:0] : 5'bz;  // Controlled_Buffer controlled_buffer_12
  assign controlled_buffer_13_out = AluSignal[11] ? Reg_A : 32'bz;  // Controlled_Buffer controlled_buffer_13
  Shifter #(.shift("lr"), .width(32)) shifter_2 (
    .in(controlled_buffer_13_out), .\dist (controlled_buffer_14_out), .out(shifter_2_out));
  assign controlled_buffer_14_out = AluSignal[11] ? Reg_B[4:0] : 5'bz;  // Controlled_Buffer controlled_buffer_14
  assign controlled_buffer_15_out = AluSignal[12] ? Reg_A : 32'bz;  // Controlled_Buffer controlled_buffer_15
  Shifter #(.shift("ar"), .width(32)) shifter_3 (
    .in(controlled_buffer_15_out), .\dist (controlled_buffer_16_out), .out(shifter_3_out));
  assign controlled_buffer_16_out = AluSignal[12] ? Reg_B[4:0] : 5'bz;  // Controlled_Buffer controlled_buffer_16
  assign controlled_buffer_17_out = AluSignal[7] ? Reg_A : 32'bz;  // Controlled_Buffer controlled_buffer_17
  assign or_2_out = controlled_buffer_17_out | controlled_buffer_18_out;  // OR_Gate or_2, 32 bits wide
  assign controlled_buffer_18_out = AluSignal[7] ? Reg_B : 32'bz;  // Controlled_Buffer controlled_buffer_18
  assign controlled_inverter_1_out = AluSignal[8] ? ~Reg_A : 32'bz;  // Controlled_Inverter controlled_inverter_1
  assign controlled_buffer_19_out = AluSignal[6] ? Reg_A : 32'bz;  // Controlled_Buffer controlled_buffer_19
  assign and_1_out = controlled_buffer_19_out & controlled_buffer_20_out;  // AND_Gate and_1, 32 bits wide
  assign controlled_buffer_20_out = AluSignal[6] ? Reg_B : 32'bz;  // Controlled_Buffer controlled_buffer_20
  assign controlled_buffer_21_out = AluSignal[9] ? Reg_B : 32'bz;  // Controlled_Buffer controlled_buffer_21
  assign Flag[0] = AluSignal[0] ? adder_1_cout : 1'bz;  // Controlled_Buffer controlled_buffer_22
  assign Flag[2] = AluSignal[1] ? subtractor_1_bout : 1'bz;  // Controlled_Buffer controlled_buffer_23
  assign Flag[0] = AluSignal[5] ? comparator_1_gt : 1'bz;  // Controlled_Buffer controlled_buffer_24
  assign Flag[1] = AluSignal[5] ? comparator_1_eq : 1'bz;  // Controlled_Buffer controlled_buffer_25
  assign Flag[2] = AluSignal[5] ? comparator_1_lt : 1'bz;  // Controlled_Buffer controlled_buffer_26
  assign Choose = AluSignal[0] ? 4'b0000 : 4'bz;  // Controlled_Buffer controlled_buffer_27
  assign Choose = AluSignal[1] ? 4'b0001 : 4'bz;  // Controlled_Buffer controlled_buffer_28
  assign Choose = AluSignal[5] ? 4'b0010 : 4'bz;  // Controlled_Buffer controlled_buffer_29
  assign Choose = AluSignal[2] ? 4'b0011 : 4'bz;  // Controlled_Buffer controlled_buffer_30
  assign Choose = AluSignal[3] ? 4'b0100 : 4'bz;  // Controlled_Buffer controlled_buffer_31
  assign Choose = AluSignal[4] ? 4'b0101 : 4'bz;  // Controlled_Buffer controlled_buffer_32
  assign Choose = AluSignal[10] ? 4'b0110 : 4'bz;  // Controlled_Buffer controlled_buffer_33
  assign Choose = AluSignal[11] ? 4'b0111 : 4'bz;  // Controlled_Buffer controlled_buffer_34
  assign Choose = AluSignal[12] ? 4'b1000 : 4'bz;  // Controlled_Buffer controlled_buffer_35
  assign Choose = AluSignal[7] ? 4'b1001 : 4'bz;  // Controlled_Buffer controlled_buffer_36
  assign Choose = AluSignal[8] ? 4'b1010 : 4'bz;  // Controlled_Buffer controlled_buffer_37
  assign Choose = AluSignal[6] ? 4'b1011 : 4'bz;  // Controlled_Buffer controlled_buffer_38
  assign Choose = AluSignal[9] ? 4'b1100 : 4'bz;  // Controlled_Buffer controlled_buffer_39
  Multiplexer #(.enable("true"), .select(4), .width(32)) multiplexer_1 (
    .in0(adder_1_out), .in1(subtractor_1_out), .in3(multiplier_1_out), .in4(divider_1_out),
    .in5(divider_1_rem), .in6(shifter_1_out), .in7(shifter_2_out), .in8(shifter_3_out), .in9(or_2_out),
    .in10(controlled_inverter_1_out), .in11(and_1_out), .in12(controlled_buffer_21_out), .out(Dout),
    .sel(Choose), .en(1'b1));  // open: in2, in13, in14, in15
  // Probe on Choose
  assign Flag[1] = AluSignal[0] ? 1'b0 : 1'bz;  // Controlled_Buffer controlled_buffer_40
  assign Flag[2] = AluSignal[0] ? 1'b0 : 1'bz;  // Controlled_Buffer controlled_buffer_41
  assign Flag[0] = AluSignal[1] ? 1'b0 : 1'bz;  // Controlled_Buffer controlled_buffer_42
  assign Flag[1] = AluSignal[1] ? 1'b0 : 1'bz;  // Controlled_Buffer controlled_buffer_43
  assign Flag[1] = AluSignal[7] ? 1'b0 : 1'bz;  // Controlled_Buffer controlled_buffer_44
  assign Flag[2] = AluSignal[7] ? 1'b0 : 1'bz;  // Controlled_Buffer controlled_buffer_45
  assign Flag[0] = AluSignal[7] ? 1'b0 : 1'bz;  // Controlled_Buffer controlled_buffer_46
  assign Flag[1] = AluSignal[8] ? 1'b0 : 1'bz;  // Controlled_Buffer controlled_buffer_47
  assign Flag[2] = AluSignal[8] ? 1'b0 : 1'bz;  // Controlled_Buffer controlled_buffer_48
  assign Flag[0] = AluSignal[8] ? 1'b0 : 1'bz;  // Controlled_Buffer controlled_buffer_49
  assign Flag[1] = AluSignal[2] ? 1'b0 : 1'bz;  // Controlled_Buffer controlled_buffer_50
  assign Flag[2] = AluSignal[2] ? 1'b0 : 1'bz;  // Controlled_Buffer controlled_buffer_51
  assign Flag[0] = AluSignal[2] ? 1'b0 : 1'bz;  // Controlled_Buffer controlled_buffer_52
  assign Flag[1] = AluSignal[10] ? 1'b0 : 1'bz;  // Controlled_Buffer controlled_buffer_53
  assign Flag[2] = AluSignal[10] ? 1'b0 : 1'bz;  // Controlled_Buffer controlled_buffer_54
  assign Flag[0] = AluSignal[10] ? 1'b0 : 1'bz;  // Controlled_Buffer controlled_buffer_55
  assign Flag[1] = AluSignal[11] ? 1'b0 : 1'bz;  // Controlled_Buffer controlled_buffer_56
  assign Flag[2] = AluSignal[11] ? 1'b0 : 1'bz;  // Controlled_Buffer controlled_buffer_57
  assign Flag[0] = AluSignal[11] ? 1'b0 : 1'bz;  // Controlled_Buffer controlled_buffer_58
  assign Flag[1] = AluSignal[6] ? 1'b0 : 1'bz;  // Controlled_Buffer controlled_buffer_59
  assign Flag[2] = AluSignal[6] ? 1'b0 : 1'bz;  // Controlled_Buffer controlled_buffer_60
  assign Flag[0] = AluSignal[6] ? 1'b0 : 1'bz;  // Controlled_Buffer controlled_buffer_61
  assign Flag[1] = AluSignal[4] ? 1'b0 : 1'bz;  // Controlled_Buffer controlled_buffer_62
  assign Flag[2] = AluSignal[4] ? 1'b0 : 1'bz;  // Controlled_Buffer controlled_buffer_63
  assign Flag[0] = AluSignal[4] ? 1'b0 : 1'bz;  // Controlled_Buffer controlled_buffer_64
  assign Flag[1] = AluSignal[11] ? 1'b0 : 1'bz;  // Controlled_Buffer controlled_buffer_65
  assign Flag[2] = AluSignal[11] ? 1'b0 : 1'bz;  // Controlled_Buffer controlled_buffer_66
  assign Flag[0] = AluSignal[11] ? 1'b0 : 1'bz;  // Controlled_Buffer controlled_buffer_67
  assign Flag[1] = AluSignal[12] ? 1'b0 : 1'bz;  // Controlled_Buffer controlled_buffer_68
  assign Flag[2] = AluSignal[12] ? 1'b0 : 1'bz;  // Controlled_Buffer controlled_buffer_69
  assign Flag[0] = AluSignal[12] ? 1'b0 : 1'bz;  // Controlled_Buffer controlled_buffer_70
  assign Flag[1] = AluSignal[9] ? 1'b0 : 1'bz;  // Controlled_Buffer controlled_buffer_71
  assign Flag[2] = AluSignal[9] ? 1'b0 : 1'bz;  // Controlled_Buffer controlled_buffer_72
  assign Flag[0] = AluSignal[9] ? 1'b0 : 1'bz;  // Controlled_Buffer controlled_buffer_73

  // Other names for the same wires on the sheet: add = AluSignal[0]; sub = AluSignal[1]; mul = AluSignal[2];
  //   div = AluSignal[3]; isMod = AluSignal[4]; cmp = AluSignal[5]; isAnd = AluSignal[6]; isOr = AluSignal[7];
  //   isNot = AluSignal[8]; mov = AluSignal[9]; Lsl = AluSignal[10]; Lsr = AluSignal[11]; Asr = AluSignal[12];
  //   C = Flag[0]; Z = Flag[1]; N = Flag[2]
endmodule

module Register_File (
  input  CLK,
  input  Reset,
  input  E,
  input  [3:0] A1,
  input  [3:0] A,
  input  [3:0] A2,
  input  [31:0] D,
  output [31:0] r0_out,
  output [31:0] D1,
  output [31:0] D2
);

  wire demultiplexer_1_out0, demultiplexer_1_out1, demultiplexer_1_out2, demultiplexer_1_out3,
       demultiplexer_1_out4, demultiplexer_1_out5, demultiplexer_1_out6, demultiplexer_1_out7,
       demultiplexer_1_out8, demultiplexer_1_out9, demultiplexer_1_out10, demultiplexer_1_out11,
       demultiplexer_1_out12, demultiplexer_1_out13, demultiplexer_1_out14, demultiplexer_1_out15;
  wire [31:0] register_2_q, register_3_q, register_4_q, register_5_q, register_6_q, register_7_q,
       register_8_q, register_9_q, register_10_q, register_11_q, register_12_q, register_13_q, register_14_q,
       register_15_q, register_16_q;

  Multiplexer #(.select(4), .width(32)) multiplexer_1 (
    .in0(r0_out), .in1(register_2_q), .in2(register_3_q), .in3(register_4_q), .in4(register_5_q),
    .in5(register_6_q), .in6(register_7_q), .in7(register_8_q), .in8(register_9_q), .in9(register_10_q),
    .in10(register_11_q), .in11(register_12_q), .in12(register_13_q), .in13(register_14_q),
    .in14(register_15_q), .in15(register_16_q), .out(D1), .sel(A1));
  Multiplexer #(.select(4), .width(32)) multiplexer_2 (
    .in0(r0_out), .in1(register_2_q), .in2(register_3_q), .in3(register_4_q), .in4(register_5_q),
    .in5(register_6_q), .in6(register_7_q), .in7(register_8_q), .in8(register_9_q), .in9(register_10_q),
    .in10(register_11_q), .in11(register_12_q), .in12(register_13_q), .in13(register_14_q),
    .in14(register_15_q), .in15(register_16_q), .out(D2), .sel(A2));
  Register #(.width(32)) register_1 (.D(D), .en(demultiplexer_1_out0), .clk(CLK), .Q(r0_out));  // open: clr
  Register #(.width(32)) register_2 (.D(D), .en(demultiplexer_1_out1), .clk(CLK), .Q(register_2_q));  // open: clr
  Register #(.width(32)) register_3 (.D(D), .en(demultiplexer_1_out2), .clk(CLK), .Q(register_3_q));  // open: clr
  Register #(.width(32)) register_4 (.D(D), .en(demultiplexer_1_out3), .clk(CLK), .Q(register_4_q));  // open: clr
  Register #(.width(32)) register_5 (.D(D), .en(demultiplexer_1_out4), .clk(CLK), .Q(register_5_q), .clr(Reset));
  Register #(.width(32)) register_6 (.D(D), .en(demultiplexer_1_out5), .clk(CLK), .Q(register_6_q), .clr(Reset));
  Register #(.width(32)) register_7 (.D(D), .en(demultiplexer_1_out6), .clk(CLK), .Q(register_7_q), .clr(Reset));
  Register #(.width(32)) register_8 (.D(D), .en(demultiplexer_1_out7), .clk(CLK), .Q(register_8_q), .clr(Reset));
  Register #(.width(32)) register_9 (.D(D), .en(demultiplexer_1_out8), .clk(CLK), .Q(register_9_q), .clr(Reset));
  Register #(.width(32)) register_10 (.D(D), .en(demultiplexer_1_out9), .clk(CLK), .Q(register_10_q), .clr(Reset));
  Register #(.width(32)) register_11 (.D(D), .en(demultiplexer_1_out10), .clk(CLK), .Q(register_11_q), .clr(Reset));
  Register #(.width(32)) register_12 (.D(D), .en(demultiplexer_1_out11), .clk(CLK), .Q(register_12_q), .clr(Reset));
  Register #(.width(32)) register_13 (.D(D), .en(demultiplexer_1_out12), .clk(CLK), .Q(register_13_q), .clr(Reset));
  Register #(.width(32)) register_14 (.D(D), .en(demultiplexer_1_out13), .clk(CLK), .Q(register_14_q), .clr(Reset));
  Register #(.width(32)) register_15 (.D(D), .en(demultiplexer_1_out14), .clk(CLK), .Q(register_15_q), .clr(Reset));
  Register #(.width(32)) register_16 (.D(D), .en(demultiplexer_1_out15), .clk(CLK), .Q(register_16_q), .clr(Reset));
  Demultiplexer #(.select(4)) demultiplexer_1 (
    .out0(demultiplexer_1_out0), .out1(demultiplexer_1_out1), .out2(demultiplexer_1_out2),
    .out3(demultiplexer_1_out3), .out4(demultiplexer_1_out4), .out5(demultiplexer_1_out5),
    .out6(demultiplexer_1_out6), .out7(demultiplexer_1_out7), .out8(demultiplexer_1_out8),
    .out9(demultiplexer_1_out9), .out10(demultiplexer_1_out10), .out11(demultiplexer_1_out11),
    .out12(demultiplexer_1_out12), .out13(demultiplexer_1_out13), .out14(demultiplexer_1_out14),
    .out15(demultiplexer_1_out15), .in(E), .sel(A));

  // Other names for the same wires on the sheet: WE = E
endmodule

module registerFilenew (
  input  CLK,
  input  Reset,
  input  E,
  input  [3:0] A1,
  input  [3:0] A,
  input  [3:0] A2,
  input  [31:0] D,
  output [31:0] r0_out,
  output [31:0] D1,
  output [31:0] D2
);

  wire demultiplexer_1_out0, demultiplexer_1_out1, demultiplexer_1_out2, demultiplexer_1_out3,
       demultiplexer_1_out4, demultiplexer_1_out5, demultiplexer_1_out6, demultiplexer_1_out7,
       demultiplexer_1_out8, demultiplexer_1_out9, demultiplexer_1_out10, demultiplexer_1_out11,
       demultiplexer_1_out12, demultiplexer_1_out13, demultiplexer_1_out14, demultiplexer_1_out15;
  wire [31:0] register_2_q, register_3_q, register_4_q, register_5_q, register_6_q, register_7_q,
       register_8_q, register_9_q, register_10_q, register_11_q, register_12_q, register_13_q, register_14_q,
       register_15_q, register_16_q;

  Multiplexer #(.select(4), .width(32)) multiplexer_1 (
    .in0(r0_out), .in1(register_2_q), .in2(register_3_q), .in3(register_4_q), .in4(register_5_q),
    .in5(register_6_q), .in6(register_7_q), .in7(register_8_q), .in8(register_9_q), .in9(register_10_q),
    .in10(register_11_q), .in11(register_12_q), .in12(register_13_q), .in13(register_14_q),
    .in14(register_15_q), .in15(register_16_q), .out(D1), .sel(A1));
  Multiplexer #(.select(4), .width(32)) multiplexer_2 (
    .in0(r0_out), .in1(register_2_q), .in2(register_3_q), .in3(register_4_q), .in4(register_5_q),
    .in5(register_6_q), .in6(register_7_q), .in7(register_8_q), .in8(register_9_q), .in9(register_10_q),
    .in10(register_11_q), .in11(register_12_q), .in12(register_13_q), .in13(register_14_q),
    .in14(register_15_q), .in15(register_16_q), .out(D2), .sel(A2));
  Register #(.width(32)) register_1 (.D(D), .en(demultiplexer_1_out0), .clk(CLK), .Q(r0_out));  // open: clr
  Register #(.width(32)) register_2 (.D(D), .en(demultiplexer_1_out1), .clk(CLK), .Q(register_2_q));  // open: clr
  Register #(.width(32)) register_3 (.D(D), .en(demultiplexer_1_out2), .clk(CLK), .Q(register_3_q));  // open: clr
  Register #(.width(32)) register_4 (.D(D), .en(demultiplexer_1_out3), .clk(CLK), .Q(register_4_q));  // open: clr
  Register #(.width(32)) register_5 (.D(D), .en(demultiplexer_1_out4), .clk(CLK), .Q(register_5_q), .clr(Reset));
  Register #(.width(32)) register_6 (.D(D), .en(demultiplexer_1_out5), .clk(CLK), .Q(register_6_q), .clr(Reset));
  Register #(.width(32)) register_7 (.D(D), .en(demultiplexer_1_out6), .clk(CLK), .Q(register_7_q), .clr(Reset));
  Register #(.width(32)) register_8 (.D(D), .en(demultiplexer_1_out7), .clk(CLK), .Q(register_8_q), .clr(Reset));
  Register #(.width(32)) register_9 (.D(D), .en(demultiplexer_1_out8), .clk(CLK), .Q(register_9_q), .clr(Reset));
  Register #(.width(32)) register_10 (.D(D), .en(demultiplexer_1_out9), .clk(CLK), .Q(register_10_q), .clr(Reset));
  Register #(.width(32)) register_11 (.D(D), .en(demultiplexer_1_out10), .clk(CLK), .Q(register_11_q), .clr(Reset));
  Register #(.width(32)) register_12 (.D(D), .en(demultiplexer_1_out11), .clk(CLK), .Q(register_12_q), .clr(Reset));
  Register #(.width(32)) register_13 (.D(D), .en(demultiplexer_1_out12), .clk(CLK), .Q(register_13_q), .clr(Reset));
  Register #(.width(32)) register_14 (.D(D), .en(demultiplexer_1_out13), .clk(CLK), .Q(register_14_q), .clr(Reset));
  Register #(.width(32)) register_15 (.D(D), .en(demultiplexer_1_out14), .clk(CLK), .Q(register_15_q), .clr(Reset));
  Register #(.width(32)) register_16 (.D(D), .en(demultiplexer_1_out15), .clk(CLK), .Q(register_16_q), .clr(Reset));
  Demultiplexer #(.select(4)) demultiplexer_1 (
    .out0(demultiplexer_1_out0), .out1(demultiplexer_1_out1), .out2(demultiplexer_1_out2),
    .out3(demultiplexer_1_out3), .out4(demultiplexer_1_out4), .out5(demultiplexer_1_out5),
    .out6(demultiplexer_1_out6), .out7(demultiplexer_1_out7), .out8(demultiplexer_1_out8),
    .out9(demultiplexer_1_out9), .out10(demultiplexer_1_out10), .out11(demultiplexer_1_out11),
    .out12(demultiplexer_1_out12), .out13(demultiplexer_1_out13), .out14(demultiplexer_1_out14),
    .out15(demultiplexer_1_out15), .in(E), .sel(A));

  // Other names for the same wires on the sheet: WE = E
endmodule
