// Logisim project CU.circ as structural Verilog
module ControlUnit (
  input  [31:0] Instruction,
  output IsImmediate,
  output [12:0] AluSignals,
  output IsLd,
  output IsSt,
  output IsBeq,
  output IsBgt,
  output IsCall,
  output IsRet,
  output IsWb,
  output IsUbranch
);

  wire and_1_out, and_2_out, and_3_out, and_4_out, demultiplexer_1_out0, demultiplexer_1_out18, nor_1_out,
       not_1_out, not_2_out, not_3_out, not_4_out, not_5_out, or_1_out, or_2_out;

  Demultiplexer #(.select(5)) demultiplexer_1 (
    .out0(demultiplexer_1_out0), .out1(AluSignals[1]), .out2(AluSignals[2]), .out3(AluSignals[3]),
    .out4(AluSignals[4]), .out5(AluSignals[5]), .out6(AluSignals[6]), .out7(AluSignals[7]),
    .out8(AluSignals[8]), .out9(AluSignals[9]), .out10(AluSignals[10]), .out11(AluSignals[11]),
    .out12(AluSignals[12]), .out14(IsLd), .out15(IsSt), .out16(IsBeq), .out17(IsBgt),
    .out18(demultiplexer_1_out18), .out19(IsCall), .out20(IsRet), .in(1'b1), .sel(Instruction[31:27]));  // open: out13, out21, out22, out23, out24, out25, out26, out27, out28, out29, out30, out31
  not not_1 (not_1_out, Instruction[27]);
  not not_2 (not_2_out, Instruction[28]);
  not not_3 (not_3_out, Instruction[29]);
  not not_4 (not_4_out, Instruction[30]);
  not not_5 (not_5_out, Instruction[31]);
  and and_1 (and_1_out, not_5_out, Instruction[30], Instruction[29], Instruction[28]);
  or or_1 (or_1_out, not_2_out, Instruction[30]);
  and and_2 (and_2_out, not_1_out, not_2_out, Instruction[29]);
  and and_3 (and_3_out, Instruction[28], not_3_out);
  or or_2 (or_2_out, and_2_out, and_3_out);
  or or_3 (AluSignals[0], demultiplexer_1_out0, and_1_out);
  and and_4 (and_4_out, Instruction[27], or_1_out, Instruction[29], not_5_out);
  nor nor_1 (nor_1_out, and_4_out, Instruction[31]);
  or or_4 (IsWb, IsCall, nor_1_out);
  and and_5 (IsUbranch, or_2_out, not_4_out, Instruction[31]);

  assign IsImmediate = Instruction[26];

  // Notes on the sheet:
  //   IsImmediate
  //   Is Add
  //   IsSub
  //   IsMul
  //   IsDiv
  //   IsMod
  //   IsCmp
  //   IsAnd
  //   IsOr
  //   IsNot
  //   IsMov
  //   IsLsl
  //   IsLsr
  //   IsAsr
  //   IsLd
  //   IsSt
  //   IsBeq
  //   IsBgt
  //   IsCall
  //   IsRet
  //   Is Add
  //   IsWb
  //   IsUbranch
endmodule
